// Logisim project I-Format-Cycle.circ as structural Verilog: 5 circuits, main circuit i-format
module i_format (
  input  [1:0] in_1,
  input  Clear,
  input  RegWrite,
  input  MemWrite,
  input  MemRead,
  input  CLK,
  output [15:0] Data,
  output [15:0] out_8,
  output [15:0] out_9,
  output [15:0] Data_2,
  output [15:0] out_11
);

  wire [1:0] adder_1_out, bit_extender_1_out, register_1_q;
  wire [15:0] register_2_read2;

  Register_part #(.width(2)) register_1 (.D(adder_1_out), .Q(register_1_q), .clk(CLK), .clr(Clear));  // open: en
  Adder #(.width(2)) adder_1 (.a(2'b01), .b(register_1_q), .out(adder_1_out));  // open: cin, cout
  ROM #(.addrWidth(2), .dataWidth(16)) rom_1 (.addr(register_1_q), .data(Data));  // open: sel
  Register register_2 (
    .Read1(out_8), .Read_1(Data[11:8]), .Read2(register_2_read2), .Write(Data[7:4]), .Data(Data_2),
    .regWrite(CLK), .regRead(RegWrite));  // open: Read_2
  Bit_Extender #(.in_width(4), .out_width(2)) bit_extender_1 (.in(Data[15:12]), .out(bit_extender_1_out));
  assign out_11 = {{12{1'b0}}, Data[3:0]};  // Bit_Extender bit_extender_2
  // ALU1 alu1_1: pin names not known; wires that end beside it: out_11, out_8, bit_extender_1_out, out_9
  Bit_Extender #(.in_width(16), .out_width(2)) bit_extender_3 (.in(out_9), .out(in_1));
  RAM #(.addrWidth(2), .dataWidth(16), .bus("separate")) ram_1 (
    .addr(in_1), .din(register_2_read2), .data(Data_2), .str(MemWrite), .clk(CLK), .ld(MemRead));  // open: sel, clr

  // Notes on the sheet:
  //   contents of rom_1 (hex, n*v repeats v):
  //   2061
endmodule

module Register (
  input  [3:0] Write,
  input  [15:0] Data,
  input  [3:0] Read_1,
  input  [3:0] Read_2,
  input  regWrite,
  input  regRead,
  output [15:0] Read1,
  output [15:0] Read2
);

  wire and_1_out, and_2_out, and_3_out, and_4_out, and_5_out, and_6_out, and_7_out, and_8_out, and_9_out,
       and_10_out, and_11_out, and_12_out, and_13_out, and_14_out, and_15_out, and_16_out, decoder_1_out0,
       decoder_1_out1, decoder_1_out2, decoder_1_out3, decoder_1_out4, decoder_1_out5, decoder_1_out6,
       decoder_1_out7, decoder_1_out8, decoder_1_out9, decoder_1_out10, decoder_1_out11, decoder_1_out12,
       decoder_1_out13, decoder_1_out14, decoder_1_out15;
  wire [15:0] register_1_q, register_2_q, register_3_q, register_4_q, register_5_q, register_6_q,
       register_7_q, register_8_q, register_9_q, register_10_q, register_11_q, register_12_q, register_13_q,
       register_14_q, register_15_q, register_16_q;

  Decoder #(.select(4)) decoder_1 (
    .out0(decoder_1_out0), .out1(decoder_1_out1), .out2(decoder_1_out2), .out3(decoder_1_out3),
    .out4(decoder_1_out4), .out5(decoder_1_out5), .out6(decoder_1_out6), .out7(decoder_1_out7),
    .out8(decoder_1_out8), .out9(decoder_1_out9), .out10(decoder_1_out10), .out11(decoder_1_out11),
    .out12(decoder_1_out12), .out13(decoder_1_out13), .out14(decoder_1_out14), .out15(decoder_1_out15),
    .sel(Write));  // open: en
  and and_1 (and_1_out, regWrite, decoder_1_out0);
  and and_2 (and_2_out, regWrite, decoder_1_out1);
  and and_3 (and_3_out, regWrite, decoder_1_out2);
  and and_4 (and_4_out, regWrite, decoder_1_out3);
  and and_5 (and_5_out, regWrite, decoder_1_out4);
  and and_6 (and_6_out, regWrite, decoder_1_out5);
  and and_7 (and_7_out, regWrite, decoder_1_out6);
  and and_8 (and_8_out, regWrite, decoder_1_out7);
  Register_part #(.width(16)) register_1 (.D(Data), .Q(register_1_q), .clk(regRead), .clr(and_1_out));  // open: en
  Register_part #(.width(16)) register_2 (.D(Data), .Q(register_2_q), .clk(regRead), .clr(and_2_out));  // open: en
  Register_part #(.width(16)) register_3 (.D(Data), .Q(register_3_q), .clk(regRead), .clr(and_3_out));  // open: en
  Register_part #(.width(16)) register_4 (.D(Data), .Q(register_4_q), .clk(regRead), .clr(and_4_out));  // open: en
  Register_part #(.width(16)) register_5 (.D(Data), .Q(register_5_q), .clk(regRead), .clr(and_5_out));  // open: en
  Register_part #(.width(16)) register_6 (.D(Data), .Q(register_6_q), .clk(regRead), .clr(and_6_out));  // open: en
  Register_part #(.width(16)) register_7 (.D(Data), .Q(register_7_q), .clk(regRead), .clr(and_7_out));  // open: en
  Register_part #(.width(16)) register_8 (.D(Data), .Q(register_8_q), .clk(regRead), .clr(and_8_out));  // open: en
  and and_9 (and_9_out, regWrite, decoder_1_out8);
  and and_10 (and_10_out, regWrite, decoder_1_out9);
  and and_11 (and_11_out, regWrite, decoder_1_out10);
  and and_12 (and_12_out, regWrite, decoder_1_out11);
  and and_13 (and_13_out, regWrite, decoder_1_out12);
  and and_14 (and_14_out, regWrite, decoder_1_out13);
  and and_15 (and_15_out, regWrite, decoder_1_out14);
  and and_16 (and_16_out, regWrite, decoder_1_out15);
  Register_part #(.width(16)) register_9 (.D(Data), .Q(register_9_q), .clk(regRead), .clr(and_9_out));  // open: en
  Register_part #(.width(16)) register_10 (.D(Data), .Q(register_10_q), .clk(regRead), .clr(and_10_out));  // open: en
  Register_part #(.width(16)) register_11 (.D(Data), .Q(register_11_q), .clk(regRead), .clr(and_11_out));  // open: en
  Register_part #(.width(16)) register_12 (.D(Data), .Q(register_12_q), .clk(regRead), .clr(and_12_out));  // open: en
  Register_part #(.width(16)) register_13 (.D(Data), .Q(register_13_q), .clk(regRead), .clr(and_13_out));  // open: en
  Register_part #(.width(16)) register_14 (.D(Data), .Q(register_14_q), .clk(regRead), .clr(and_14_out));  // open: en
  Register_part #(.width(16)) register_15 (.D(Data), .Q(register_15_q), .clk(regRead), .clr(and_15_out));  // open: en
  Register_part #(.width(16)) register_16 (.D(Data), .Q(register_16_q), .clk(regRead), .clr(and_16_out));  // open: en
  Multiplexer #(.select(4), .width(16)) multiplexer_1 (
    .in0(register_9_q), .in1(register_10_q), .in2(register_11_q), .in3(register_12_q), .in4(register_13_q),
    .in5(register_14_q), .in6(register_15_q), .in7(register_16_q), .in8(register_1_q), .in9(register_2_q),
    .in10(register_3_q), .in11(register_4_q), .in12(register_5_q), .in13(register_6_q), .in14(register_7_q),
    .in15(register_8_q), .out(Read1), .sel(Read_1));  // open: en
  Multiplexer #(.select(4), .width(16)) multiplexer_2 (
    .in0(register_9_q), .in1(register_10_q), .in2(register_11_q), .in3(register_12_q), .in4(register_13_q),
    .in5(register_14_q), .in6(register_15_q), .in7(register_16_q), .in8(register_1_q), .in9(register_2_q),
    .in10(register_3_q), .in11(register_4_q), .in12(register_5_q), .in13(register_6_q), .in14(register_7_q),
    .in15(register_8_q), .out(Read2), .sel(Read_2));  // open: en
endmodule

module ALU (
  input  CarryIn,
  input  A,
  input  [1:0] Operation,
  input  B,
  input  Binvert,
  output Result,
  output CarryOut
);

  wire adder_1_out, and_1_out, multiplexer_1_out, not_1_out, or_1_out;

  not not_1 (not_1_out, B);
  Multiplexer multiplexer_1 (.in0(B), .in1(not_1_out), .out(multiplexer_1_out), .sel(Binvert));  // open: en
  and and_1 (and_1_out, A, multiplexer_1_out);
  or or_1 (or_1_out, A, multiplexer_1_out);
  Adder #(.width(1)) adder_1 (.a(A), .b(multiplexer_1_out), .out(adder_1_out), .cin(CarryIn), .cout(CarryOut));
  Multiplexer #(.select(2)) multiplexer_2 (
    .in0(and_1_out), .in1(or_1_out), .in2(adder_1_out), .out(Result), .sel(Operation));  // open: in3, en
endmodule

// ALU-16Bit
module ALU_16bit (
  input  CarryIn,
  input  [15:0] A,
  input  [15:0] B,
  input  [1:0] Operation,
  input  Binvert,
  output zero,
  output [15:0] Result,
  output Overflow,
  output Carry
);

  wire alu_1_carryout, alu_2_carryout, alu_3_carryout, alu_4_carryout, alu_5_carryout, alu_6_carryout,
       alu_7_carryout, alu_8_carryout, alu_9_carryout, alu_10_carryout, alu_11_carryout, alu_12_carryout,
       alu_13_carryout, alu_14_carryout, alu_15_carryout;

  ALU alu_1 (
    .Result(Result[15]), .CarryOut(alu_1_carryout), .B(B[0]), .A(A[0]), .CarryIn(CarryIn), .Binvert(Binvert),
    .Operation(Operation));
  ALU alu_2 (
    .Result(Result[15]), .CarryOut(alu_2_carryout), .B(B[1]), .A(A[1]), .CarryIn(alu_1_carryout),
    .Binvert(Binvert), .Operation(Operation));
  ALU alu_3 (
    .Result(Result[15]), .CarryOut(alu_3_carryout), .B(B[2]), .A(A[2]), .CarryIn(alu_2_carryout),
    .Binvert(Binvert), .Operation(Operation));
  ALU alu_4 (
    .Result(Result[15]), .CarryOut(alu_4_carryout), .B(B[3]), .A(A[3]), .CarryIn(alu_3_carryout),
    .Binvert(Binvert), .Operation(Operation));
  ALU alu_5 (
    .Result(Result[15]), .CarryOut(alu_5_carryout), .B(B[4]), .A(A[4]), .CarryIn(alu_4_carryout),
    .Binvert(Binvert), .Operation(Operation));
  ALU alu_6 (
    .Result(Result[15]), .CarryOut(alu_6_carryout), .B(B[5]), .A(A[5]), .CarryIn(alu_5_carryout),
    .Binvert(Binvert), .Operation(Operation));
  ALU alu_7 (
    .Result(Result[15]), .CarryOut(alu_7_carryout), .B(B[6]), .A(A[6]), .CarryIn(alu_6_carryout),
    .Binvert(Binvert), .Operation(Operation));
  ALU alu_8 (
    .Result(Result[15]), .CarryOut(alu_8_carryout), .B(B[7]), .A(A[7]), .CarryIn(alu_7_carryout),
    .Binvert(Binvert), .Operation(Operation));
  ALU alu_9 (
    .Result(Result[15]), .CarryOut(alu_9_carryout), .B(B[8]), .A(A[8]), .CarryIn(alu_8_carryout),
    .Binvert(Binvert), .Operation(Operation));
  ALU alu_10 (
    .Result(Result[15]), .CarryOut(alu_10_carryout), .B(B[9]), .A(A[9]), .CarryIn(alu_9_carryout),
    .Binvert(Binvert), .Operation(Operation));
  ALU alu_11 (
    .Result(Result[15]), .CarryOut(alu_11_carryout), .B(B[10]), .A(A[10]), .CarryIn(alu_10_carryout),
    .Binvert(Binvert), .Operation(Operation));
  ALU alu_12 (
    .Result(Result[15]), .CarryOut(alu_12_carryout), .B(B[11]), .A(A[11]), .CarryIn(alu_11_carryout),
    .Binvert(Binvert), .Operation(Operation));
  ALU alu_13 (
    .Result(Result[15]), .CarryOut(alu_13_carryout), .B(B[12]), .A(A[12]), .CarryIn(alu_12_carryout),
    .Binvert(Binvert), .Operation(Operation));
  ALU alu_14 (
    .Result(Result[15]), .CarryOut(alu_14_carryout), .B(B[13]), .A(A[13]), .CarryIn(alu_13_carryout),
    .Binvert(Binvert), .Operation(Operation));
  ALU alu_15 (
    .Result(Result[15]), .CarryOut(alu_15_carryout), .B(B[14]), .A(A[14]), .CarryIn(alu_14_carryout),
    .Binvert(Binvert), .Operation(Operation));
  ALU alu_16 (
    .Result(Result[15]), .CarryOut(Carry), .B(B[15]), .A(A[15]), .CarryIn(alu_15_carryout),
    .Binvert(Binvert), .Operation(Operation));
  xor xor_1 (Overflow, alu_15_carryout, Carry);
  nor nor_1 (zero, Result[15], Result[15], Result[15], Result[15], Result[15], Result[15], Result[15], Result[15], Result[15], Result[15], Result[15], Result[15], Result[15], Result[15], Result[15], Result[15]);

  assign Result[14:0] = {15{Result[15]}};
endmodule

// ALU
module ALU1 (
  input  CarryIn,
  input  [15:0] A,
  input  [15:0] B,
  input  [1:0] Operation,
  input  Binvert,
  output zero,
  output [15:0] Result,
  output out_8,
  output out_9
);

  // ALU_16bit alu_16bit_1: pin names not known; wires that end beside it: A, B, Operation, Binvert, CarryIn, zero, Result, out_8, out_9
endmodule
